# Fritzing sketch Lighting Circuit Diagram (saved by Fritzing 0.9.3b)
breadboards: 1

parts:
  M2 = Stepper Motor - Bipolar  # not connected
  VCC2 = Battery block 9V
  R3 = PHOTOCELL [package=photocell-kit]
  R4 = Resistor [tolerance=±5% resistance=220 package="2010 [SMD]"]
  A1 = Arduino UNO R4 WiFi
  S1 = H-Bridge with L298N

nets:
  N1: VCC2.-, R4.Pin_0, A1.Pin_2, A1.Pin_9
  N2: VCC2.+, R3.P$2
  N3: R3.P$1, R4.Pin_1, A1.Pin_12
  N4: A1.Pin_42, S1.IN1
  N5: A1.Pin_43, S1.IN2
  N6: A1.Pin_44, S1.IN3
  N7: A1.Pin_45, S1.IN4

custom parts:
  Arduino UNO R4 WiFi: The Arduino UNO R4 WiFi merges the RA4M1 microprocessor from Renesas with the ESP32-S3 from Espressif, creating an all-in-one tool for makers with enhanced processing power and a diverse array of new peripherals.
  H-Bridge with L298N: h-bridge
